// Logisim project Normal.circ as structural Verilog: 1 circuit, main circuit main
module main (
  input  A,
  input  B,
  input  C,
  input  D,
  output out_5,
  output out_6,
  output out_7,
  output out_8,
  output out_9
);

  wire and_1_out, and_2_out, and_3_out, and_4_out, and_5_out, and_6_out, and_7_out, and_8_out;

  and and_1 (and_1_out, ~A, ~B, D);  // AND_Gate
  and and_2 (and_2_out, ~B, C);  // AND_Gate
  and and_3 (and_3_out, B, ~C);  // AND_Gate
  and and_4 (and_4_out, C, ~D);  // AND_Gate
  and and_5 (and_5_out, C, D);
  and and_6 (and_6_out, A, ~D);  // AND_Gate
  and and_7 (and_7_out, B, D);
  and and_8 (and_8_out, B, C);
  or or_1 (out_5, and_1_out, and_2_out, and_3_out);
  or or_2 (out_6, and_2_out, and_3_out, and_4_out);
  or or_3 (out_7, B, and_5_out);
  or or_4 (out_8, B, and_6_out);
  or or_5 (out_9, A, and_7_out, and_8_out);
endmodule
